# Fritzing sketch ESP8266-shiftregister (saved by Fritzing 0.9.3b)
circuit board: 8.46667cm x 5.64444cm
breadboards: 1

parts:
  U1 = ESP8266 WiFi Module [part_number=ESP8266]  # not connected
  U2 = 74HC595 [package="DIP16 [THT]"]
  J1 = Camdenboss CTB0158-4 [part_number=CTB0158-4 package=THT]

nets:
  N1: U2.Q1, J1.pin3
  N2: U2.Q2, J1.pin2
  N3: U2.Q3, J1.pin1
  N4: U2.Q0, J1.pin4

custom parts:
  ESP8266 WiFi Module: Generic WiFi Module based on the ESP8266 with onboard PCB antenna and UART communications
